# Fritzing sketch schematics (saved by Fritzing 0.9.3b)
circuit board: 13.545cm x 9.58702cm
breadboards: 1

parts:
  Bauteil2 = Arduino Nano (Rev3.0)
  OLED1 = OLED 128x64 I2C Monochrome Display
  XLR1 = XLR3_NCFAH2 [package=xlr3_nc3fah2]
  XLR2 = XLR3_NCFAH2 [package=xlr3_nc3fah2]
  AMPHENOL_-_ACJS-MHDR_-_JACK_6_35MM1 = AMPHENOL - ACJS-MHDR [package=ACJS-MHDR]
  AMPHENOL_-_ACJS-MHDR_-_JACK_6_35MM2 = AMPHENOL - ACJS-MHDR [package=ACJS-MHDR]
  D3 = Diode [package=diode-1n4148]
  D4 = Diode [package=diode-1n4148]
  D5 = Diode [package=diode-1n4148]
  S3 = SPST Switch [package=switch-spdt-smd]
  S4 = Pushbutton [package="[THT]"]
  S5 = SWITCH-DPDT [package=gpi-152-3013]
  VCC1 = Battery block 9V
  J1 = female pin header, 4 pins [form="♀ (female)"]
  J2 = female pin header, 4 pins [form="♀ (female)"]
  D6 = Diode [package=diode-1n4148]

nets (from the pcb view):
  GND: Bauteil2.GND, OLED1.GND, S3.S, S4.Pin_3, S4.Pin_4, S5.4, VCC1.-
  N1: Bauteil2.D2, S4.Pin_1, S4.Pin_2
  N2: Bauteil2.D3, D6.C
  N3: Bauteil2.D4, D3.C
  N4: Bauteil2.D5, D5.C
  N5: Bauteil2.D6, D4.C
  N6: Bauteil2.D7, AMPHENOL_-_ACJS-MHDR_-_JACK_6_35MM1.Tip_(6)
  N7: Bauteil2.D8, AMPHENOL_-_ACJS-MHDR_-_JACK_6_35MM1.Ring_(5)
  N8: Bauteil2.D9, AMPHENOL_-_ACJS-MHDR_-_JACK_6_35MM1.Sleeve_(4)
  N9: Bauteil2.D10, J2.pin4
  N10: Bauteil2.VIN, S5.1, S5.3
  5V: Bauteil2.5V, OLED1.VDD
  N11: Bauteil2.A5, OLED1.SCK
  N12: Bauteil2.A4, OLED1.SDA
  N13: Bauteil2.A1, S3.O
  N14: Bauteil2.A0, S3.P
  N15: XLR1.1, AMPHENOL_-_ACJS-MHDR_-_JACK_6_35MM1.Sleeve_(1), J2.pin3
  N16: XLR1.2, AMPHENOL_-_ACJS-MHDR_-_JACK_6_35MM1.Ring_(2), J2.pin2
  N17: XLR1.3, AMPHENOL_-_ACJS-MHDR_-_JACK_6_35MM1.Tip_(3), J2.pin1
  N18: XLR2.1, AMPHENOL_-_ACJS-MHDR_-_JACK_6_35MM2.Sleeve_(4), J1.pin3
  N19: XLR2.2, AMPHENOL_-_ACJS-MHDR_-_JACK_6_35MM2.Ring_(5), J1.pin2
  N20: XLR2.3, AMPHENOL_-_ACJS-MHDR_-_JACK_6_35MM2.Tip_(6), J1.pin1
  N21: AMPHENOL_-_ACJS-MHDR_-_JACK_6_35MM2.Sleeve_(1), D3.A
  N22: AMPHENOL_-_ACJS-MHDR_-_JACK_6_35MM2.Ring_(2), D5.A
  N23: AMPHENOL_-_ACJS-MHDR_-_JACK_6_35MM2.Tip_(3), D4.A
  N24: S5.2, VCC1.+
  N25: J1.pin4, D6.A

notes:
  Klinke 6.35mm
  XLR
  SpeakOn
  Channel Selector
  Mode Selector
